// Logisim project crs165_proj2.circ as structural Verilog: 6 circuits, main circuit main
// reg file
module main (
  input  [15:0] data,
  output enable,
  output ALUBsrc,
  output [2:0] aluop,
  output [2:0] out_5,
  output out_6,
  output out_7,
  output out_8,
  output out_9,
  output out_10,
  output out_11,
  output out_12,
  output out_13,
  output out_14,
  output out_15,
  output out_16
);

  wire branch, clk_out, clock_1_out, Halt, jal, jr_rs, jump, step_out, \type ;
  wire [2:0] rd, rs, rt;
  wire [3:0] first, fourth, second, third;
  wire [6:0] keyboard_1_data, multiplexer_1_out;
  wire [7:0] adder_1_out, bit_extender_1_out, bit_extender_2_out, multiplexer_3_out, PC_out;
  wire [15:0] alu, bit_extender_4_out, imm, keyboard_out, multiplexer_2_out, multiplexer_5_out, Ram_Output,
       rs_out, rt_out;
  wire [19:0] rom_1_data;

  LED led_1 (.in(Halt));
  // Probe on rs_out
  Hex_Digit_Display hex_digit_display_1 (.value(second));  // open: dp
  Hex_Digit_Display hex_digit_display_2 (.value(first));  // open: dp
  Button step (.out(step_out));
  or or_1 (clk_out, step_out, clock_1_out);
  Clock clock_1 (.out(clock_1_out));
  Multiplexer #(.width(7)) multiplexer_1 (
    .in0(rs_out[6:0]), .in1(imm[6:0]), .out(multiplexer_1_out), .sel(out_10));  // open: en
  Hex_Digit_Display hex_digit_display_3 (.value(third));  // open: dp
  Hex_Digit_Display hex_digit_display_4 (.value(fourth));  // open: dp
  // Probe on {first, second, third, fourth}
  Register #(.width(16)) register_1 (
    .D(rs_out), .en(enable), .Q({first, second, third, fourth}), .clk(clk_out));  // open: clr
  TTY tty_1 (.data(multiplexer_1_out), .clk(clk_out), .we(out_8));  // open: clr
  Multiplexer #(.width(16)) multiplexer_2 (
    .in0(rt_out), .in1(imm), .out(multiplexer_2_out), .sel(ALUBsrc));  // open: en
  Bit_Extender #(.in_width(16), .out_width(8), .\type ("sign")) bit_extender_1 (.in(imm), .out(bit_extender_1_out));
  ALU alu_1 (.A(rs_out), .B(multiplexer_2_out), .op(aluop), .out_4(alu));
  Keyboard keyboard_1 (.clk(clk_out), .re(out_9), .data(keyboard_1_data));  // open: clr, avail
  Bit_Extender #(.in_width(16), .out_width(8)) bit_extender_2 (.in(rs_out), .out(bit_extender_2_out));
  PC pc_1 (
    .halt(Halt), .imm8(bit_extender_1_out), .clk(clk_out), .rs(bit_extender_2_out), .blt(out_16),
    .bget(out_13), .beq(out_14), .bne(out_15), .jr_rs(jr_rs), .Jump(jump), .out_11(PC_out));
  Adder adder_1 (.a(PC_out), .b(8'h1), .out(adder_1_out));  // open: cin, cout
  ROM #(.dataWidth(20)) rom_1 (.addr(PC_out), .data(rom_1_data), .sel(1'b1));
  assign keyboard_out = {{9{1'b0}}, keyboard_1_data};  // Bit_Extender bit_extender_3
  Multiplexer #(.width(8)) multiplexer_3 (
    .in0(PC_out), .in1(adder_1_out), .out(multiplexer_3_out), .sel(jal));  // open: en
  Multiplexer #(.width(16)) multiplexer_4 ();  // open: in0, in1, out, sel, en
  assign bit_extender_4_out = {{8{1'b0}}, multiplexer_3_out};  // Bit_Extender bit_extender_4
  Control control_1 (
    .Instruction(rom_1_data), .Halt(Halt), .Enable_out(enable), .rd(rd), .rs(rs), .rt(rt), .Ram_Write(out_7),
    .AlubSrc(ALUBsrc), .aluop(aluop), .Jump(jump), .Branch(branch), .jr_rs(jr_rs), .imm(imm), .RegSrc(out_5),
    .regwrite(out_6), .tty_source(out_10), .tty_write(out_8), .keyboard_write(out_9), .lui_write(out_11),
    .r_type(\type ), .bgez_type(out_13), .bequal_type(out_14), .bbnezl_type(out_15), .blt(out_16), .jal(jal));
  Multiplexer #(.select(3), .width(16)) multiplexer_5 (
    .in0(alu), .in1(Ram_Output), .in2(imm), .in3(bit_extender_4_out), .in4(keyboard_out),
    .out(multiplexer_5_out), .sel(out_5));  // open: in5, in6, in7, en
  Reg_File reg_file_1 (
    .Data(multiplexer_5_out), .WE(out_6), .CLK(clk_out), .rs_out(rs_out), .rt_out(rt_out), .rd(rd), .rs(rs),
    .rt(rt));
  RAM #(.addrWidth(16), .dataWidth(16), .bus("separate")) ram_1 (
    .addr(alu), .din(rt_out), .data(Ram_Output), .str(out_7), .clk(clk_out));  // open: sel, ld, clr

  // Other names for the same wires on the sheet: bequals = out_14; bgez = out_13; blt = out_16; bne = out_15;
  //   data_out[15:0] = data; enable_out = enable; keyboard_write = out_9; lui_write = out_11; r_type = out_12;
  //   Ram_write = out_7; RegSrc[2:0] = out_5; regwrite = out_6; tty_src = out_10; tty_write = out_8

  // Notes on the sheet:
  //   Instant Memory
  //   contents of rom_1 (hex, n*v repeats v):
  //   88802 4100 88803 89003 1e140 d8407 b5900 1db40 d8305 d43fe b5202 cc004 4100 b4902 cc003
  //   Data Memory
endmodule

// pc
module PC (
  input  halt,
  input  [7:0] imm8,
  input  clk,
  input  [7:0] rs,
  input  Jump,
  input  jr_rs,
  input  blt,
  input  bget,
  input  beq,
  input  bne,
  output [7:0] out_11
);

  wire and_1_out, and_2_out, and_3_out, and_4_out, bge, equal, greater, halt_output, if_condition, less_than,
       not_2_p1, not_3_out, or_1_out, or_2_out, or_4_out, or_6_out;
  wire [7:0] adder_1_out, multiplexer_1_out, multiplexer_2_out, multiplexer_3_out;

  and and_1 (and_1_out, blt, less_than);
  // Probe on imm8
  // Probe on rs
  and and_2 (and_2_out, or_1_out, bget);
  or or_1 (or_1_out, greater, equal);
  // NOT_Gate not_1: pin names not known; wires that end beside it: halt, halt_output
  Multiplexer #(.width(8)) multiplexer_1 (.in0(8'h1), .in1(imm8), .out(multiplexer_1_out), .sel(or_2_out));  // open: en
  or or_2 (or_2_out, and_1_out, and_2_out, and_4_out, and_3_out);
  and and_3 (and_3_out, not_2_p1, bne);
  and and_4 (and_4_out, equal, beq);
  // NOT_Gate not_2: pin names not known; wires that end beside it: not_2_p1, equal, bne
  Adder adder_1 (.a(out_11), .b(multiplexer_1_out), .out(adder_1_out));  // open: cin, cout
  Multiplexer #(.width(8)) multiplexer_2 (
    .in0(adder_1_out), .in1(rs), .out(multiplexer_2_out), .sel(jr_rs));  // open: en
  Multiplexer #(.width(8)) multiplexer_3 (
    .in0(multiplexer_2_out), .in1(imm8), .out(multiplexer_3_out), .sel(Jump));  // open: en
  Register PC (.D(multiplexer_3_out), .en(halt_output), .Q(out_11), .clk(clk));  // open: clr
  // Probe on out_11
  or or_3 (bge, greater, equal);
  not not_3 (not_3_out, equal);
  Comparator comparator_1 (.a(rs), .b({8{1'b0}}), .gt(greater), .eq(equal), .lt(less_than));
  or or_4 (or_4_out, equal, not_3_out);
  or or_5 (if_condition, or_4_out, or_6_out);
  or or_6 (or_6_out, less_than, greater);

  // Other names for the same wires on the sheet: bge_t = bget; i[7:0] = out_11; imm8_out[7:0] = imm8
endmodule

module ALU (
  input  [15:0] A,
  input  [15:0] B,
  input  [2:0] op,
  output [15:0] out_4
);

  wire [15:0] and_out, left__out, not_out, or_out, out, out_t, right__out;

  // Probe on A
  // Probe on B
  Adder #(.width(16)) adder_1 (.a(A), .b(B), .out(out));  // open: cin, cout
  Subtractor #(.width(16)) subtractor_1 (.a(A), .b(B), .out(out_t));  // open: bin, bout
  assign and_out = A & B;  // AND_Gate and_1, 16 bits wide
  assign or_out = A | B;  // OR_Gate or_1, 16 bits wide
  // NOT_Gate #(.width(16)) not_1: pin names not known; wires that end beside it: A, not_out
  Shifter #(.width(16)) shifter_1 (.in(A), .\dist (B[3:0]), .out(left__out));
  Shifter #(.width(16), .shift("lr")) shifter_2 (.in(A), .\dist (B[3:0]), .out(right__out));
  Multiplexer #(.select(3), .width(16)) multiplexer_1 (
    .in0(out), .in1(out_t), .in2(and_out), .in3(or_out), .in4(not_out), .in5(left__out), .in6(right__out),
    .out(out_4), .sel(op));  // open: in7, en
  // Probe on op
  // Probe on out_4

  // Other names for the same wires on the sheet: A_out[15:0] = A; B_out[15:0] = B

  // Notes on the sheet:
  //   0 = +
  //   1 = -
  //   2 = and
  //   3 = or
  //   4 = not
  //   5 = left
  //   6 = right
endmodule

module Reg_File (
  input  [15:0] Data,
  input  WE,
  input  CLK,
  input  [2:0] rs,
  input  [2:0] rd,
  input  [2:0] rt,
  output [15:0] rs_out,
  output [15:0] rt_out
);

  wire demultiplexer_1_out0, r1_in, r2_in, r3_in, r4_in, r5_in, r6_in, r7_in;
  wire [15:0] r1_out, r2_out, r3_out, r4_out, r5_out, r6_out, r7_out;

  Demultiplexer #(.select(3)) demultiplexer_1 (
    .out0(demultiplexer_1_out0), .out1(r1_in), .out2(r2_in), .out3(r3_in), .out4(r4_in), .out5(r5_in),
    .out6(r6_in), .out7(r7_in), .in(WE), .sel(rd));  // open: en
  Register #(.width(16)) _1__r1 (.D(Data), .en(r1_in), .Q(r1_out), .clk(CLK));  // open: clr
  Register #(.width(16)) _3__r3 (.D(Data), .en(r3_in), .Q(r3_out), .clk(CLK));  // open: clr
  Register #(.width(16)) _4__r4 (.D(Data), .en(r4_in), .Q(r4_out), .clk(CLK));  // open: clr
  Register #(.width(16)) _5__r5 (.D(Data), .en(r5_in), .Q(r5_out), .clk(CLK));  // open: clr
  Register #(.width(16)) _6__r6 (.D(Data), .en(r6_in), .Q(r6_out), .clk(CLK));  // open: clr
  Register #(.width(16)) _7__r7 (.D(Data), .en(r7_in), .Q(r7_out), .clk(CLK));  // open: clr
  Register #(.width(16)) _2__r2 (.D(Data), .en(r2_in), .Q(r2_out), .clk(CLK));  // open: clr
  Multiplexer #(.select(3), .width(16)) multiplexer_1 (
    .in0({16{1'b0}}), .in1(r1_out), .in2(r2_out), .in3(r3_out), .in4(r4_out), .in5(r5_out), .in6(r6_out),
    .in7(r7_out), .out(rs_out), .sel(rs));  // open: en
  Multiplexer #(.select(3), .width(16)) multiplexer_2 (
    .in0({16{1'b0}}), .in1(r1_out), .in2(r2_out), .in3(r3_out), .in4(r4_out), .in5(r5_out), .in6(r6_out),
    .in7(r7_out), .out(rt_out), .sel(rt));  // open: en
  // Probe on rs_out
  // Probe on rt

  // Other names for the same wires on the sheet: Data_out[15:0] = Data; We_out = WE
endmodule

module Control (
  input  [19:0] Instruction,
  output Halt,
  output Enable_out,
  output [2:0] rd,
  output [2:0] rs,
  output [2:0] rt,
  output Ram_Write,
  output AlubSrc,
  output [2:0] aluop,
  output Jump,
  output Branch,
  output jr_rs,
  output [15:0] imm,
  output [2:0] RegSrc,
  output regwrite,
  output tty_source,
  output tty_write,
  output keyboard_write,
  output lui_write,
  output r_type,
  output bgez_type,
  output bequal_type,
  output bbnezl_type,
  output blt,
  output jal
);

  wire add, adi, \and , and_1_out, and_2_out, ani, j, ld, li, \not , \or , or_2_out, or_3_out, or_4_p3,
       or_5_p3, or_6_out, or_7_out, or_8_out, or_10_out, or_11_out, or_12_out, or_17_out, or_18_out, ori,
       out, sbi, shl, shr, sli, sri, st, sub, z1, z2;
  wire [4:0] multiplexer_1_out, multiplexer_2_out;
  wire [7:0] multiplexer_3_out, multiplexer_4_out;
  wire [15:0] bit_extender_1_out, bit_extender_2_out, bit_extender_3_out, bit_extender_4_out, lui_imm,
       mux_out, t1, t2;

  // OR_Gate or_1 has open pins: in0=add, in1=add, in2=adi, in3=st, out=open
  or or_2 (or_2_out, \and , ani);
  or or_3 (or_3_out, \or , ori);
  // OR_Gate or_4: pin names not known; wires that end beside it: sub, sbi, or_4_p3
  // OR_Gate or_5: pin names not known; wires that end beside it: shl, sli, or_5_p3
  or or_6 (or_6_out, shr, sri);
  or or_7 (or_7_out, lui_write, blt, bgez_type, sli, jr_rs, tty_source, li, j, ani, ori, keyboard_write, sri, bequal_type, jal, bbnezl_type);
  buf or_8 (or_8_out, Instruction[19]);  // OR_Gate
  or or_9 (z2, adi, sbi);
  or or_10 (or_10_out, adi, sbi);
  buf or_11 (or_11_out, Instruction[19]);  // OR_Gate
  or or_12 (or_12_out, li, lui_write);
  // Decoder #(.select(5)) decoder_1: pin names not known; wires that end beside it: Instruction[18:14], Halt, Enable_out, li, lui_write, st, ld, add, sub, \and , \or , \not , shl, shr, adi, sbi, ani, ori, sli, sri, j, blt, bgez_type, bequal_type, bbnezl_type, jal, jr_rs, out, tty_source, keyboard_write
  buf or_13 (Ram_Write, st);  // OR_Gate
  Priority_Encoder priority_encoder_1 (
    .in0(1'b1), .in1(or_4_p3), .in2(or_2_out), .in3(or_3_out), .in4(\not ), .in5(or_5_p3), .in6(or_6_out),
    .out(aluop));  // open: in7, en_in, gs, en_out
  or or_14 (Jump, j, jal);
  buf or_15 (Branch, blt);  // OR_Gate
  or or_16 (z1, sri, ld, li, st, ani, ori, keyboard_write, sli, lui_write);
  and and_1 (and_1_out, or_7_out, or_8_out);
  and and_2 (and_2_out, or_10_out, or_11_out);
  or or_17 (or_17_out, st, ld);
  buf or_18 (or_18_out, jal);  // OR_Gate
  or or_19 (regwrite, li, st, add, \and , \not , shr, sbi, ori, sri, blt, bequal_type, jal, out, keyboard_write, Enable_out, lui_write, ld, sub, \or , shl, adi, ani, sli, bgez_type, bbnezl_type, jr_rs, tty_source);
  or or_20 (tty_write, tty_source, out);
  Multiplexer #(.width(5)) multiplexer_1 (
    .in0(5'b00001), .in1(Instruction[4:0]), .out(multiplexer_1_out), .sel(z1));  // open: en
  Multiplexer #(.width(5)) multiplexer_2 (.in0(Instruction[4:0]), .out(multiplexer_2_out), .sel(z2));  // open: in1, en
  or or_21 (AlubSrc, ld, adi, sbi, ani, ori, sli, sri, st);
  assign bit_extender_1_out = {{11{1'b0}}, multiplexer_1_out};  // Bit_Extender bit_extender_1
  Multiplexer #(.width(8)) multiplexer_3 (
    .in0(8'h1), .in1(Instruction[7:0]), .out(multiplexer_3_out), .sel(and_1_out));  // open: en
  assign bit_extender_2_out = {{11{multiplexer_2_out[4]}}, multiplexer_2_out};  // Bit_Extender bit_extender_2
  Multiplexer #(.width(8)) multiplexer_4 (
    .in0(8'h1), .in1(Instruction[7:0]), .out(multiplexer_4_out), .sel(and_2_out));  // open: en
  Priority_Encoder priority_encoder_2 (
    .in0(1'b1), .in1(or_17_out), .in2(or_12_out), .in3(or_18_out), .in4(keyboard_write), .out(RegSrc));  // open: in5, in6, in7, en_in, gs, en_out
  assign bit_extender_3_out = {{8{1'b0}}, multiplexer_3_out};  // Bit_Extender bit_extender_3
  assign bit_extender_4_out = {{8{multiplexer_4_out[7]}}, multiplexer_4_out};  // Bit_Extender bit_extender_4
  Multiplexer #(.width(16)) multiplexer_5 (
    .in0(bit_extender_1_out), .in1(bit_extender_3_out), .out(t1), .sel(Instruction[19]));  // open: en
  Multiplexer #(.width(16)) multiplexer_6 (
    .in0(bit_extender_2_out), .in1(bit_extender_4_out), .out(t2), .sel(Instruction[19]));  // open: en
  Multiplexer #(.width(16)) multiplexer_7 (.in0(t1), .in1(t2), .out(mux_out), .sel(z2), .en(z2));
  lui_shifter lui_shifter_1 (.lui_write(lui_write), .\input (mux_out), .lui_imm(lui_imm));
  Multiplexer #(.width(16)) multiplexer_8 (.in0(mux_out), .in1(lui_imm), .out(imm), .sel(lui_write));  // open: en
  // Probe on imm

  assign r_type = Instruction[19];
  assign rd = Instruction[13:11];
  assign rs = Instruction[10:8];
  assign rt = Instruction[7:5];

  // Other names for the same wires on the sheet: beqz = bequal_type; bgez = bgez_type; bltz = blt; bnez = bbnezl_type;
  //   hlt = Halt; in = keyboard_write; imm5[4:0] = Instruction[4:0]; imm8[7:0] = Instruction[7:0];
  //   opcode[4:0] = Instruction[18:14]; jr = jr_rs; lui = lui_write; oui = tty_source; put = Enable_out

  // Notes on the sheet:
  //   zero extension
  //   sign extension
  //   sign extension
endmodule

module lui_shifter (
  input  lui_write,
  input  [15:0] \input ,
  output [15:0] lui_imm
);

  Shifter #(.width(16)) shifter_1 (.in(\input ), .\dist (4'b1000), .out(lui_imm));
endmodule
